# Fritzing sketch Atmega328p (saved by Fritzing 0.7.12b)
breadboards: 1

parts:
  Digital-3 = female pin header, 5 pins [form="♀ (female)"]  # not connected
  I2C = female pin header, 5 pins [form="♀ (female)"]
  Digital-2 = female pin header, 5 pins [form="♀ (female)"]  # not connected
  Analog-2 = female pin header, 5 pins [form="♀ (female)"]  # not connected
  LED1 = LED - 5mm [color="Red (633nm)" package="5 mm [THT]"]
  R3 = Resistor [tolerance=±5% resistance=1k package="0805 [SMD]"]
  R2 = Resistor [tolerance=±5% resistance=2.2k package="0805 [SMD]"]
  R7 = Resistor [tolerance=±5% resistance=220 package="0805 [SMD]"]
  Digital-1 = female pin header, 5 pins [form="♀ (female)"]  # not connected
  5V = female pin header, 2 pins [form="♀ (female)"]  # not connected
  U1 = atmega328 [package=dip]  # not connected
  Analog-1 = female pin header, 5 pins [form="♀ (female)"]  # not connected
  5V_2 = female pin header, 2 pins [form="♀ (female)"]  # not connected
  R8 = Resistor [tolerance=±5% resistance=1k package="0805 [SMD]"]  # not connected

nets:
  N1: I2C.pin2, R3.Pin_1, R2.Pin_1
  N2: I2C.pin5, R2.Pin_0
  N3: LED1.anode, R7.Pin_0

notes:
  +
  -
  *
  i
  o
  d
  c
  Analog 1
  Analog 2
  o - D5 (PWM)
  i - A0 (ADC)
  o - D9 (PWM)
  i - A1 (ADC)
  Digital 1
  Digital 2
  Digital 3
  i - D4
  o - D3
  i - D12
  o - D13
  i - D10
  o - D8 (3.3v)
  I2C
  SDA - A4
  * - D2
  SCL - A5
  clixx.io
  * - D11
  * - D6 (PWM)

// code stored in the sketch: toneMelody.ino
/*
  Melody
 
 Plays a melody 
 
 circuit:
 * 8-ohm speaker on digital pin 8
 
 created 21 Jan 2010
 modified 30 Aug 2011
 by Tom Igoe 

This example code is in the public domain.
 
 http://arduino.cc/en/Tutorial/Tone
 
 */
 #include "pitches.h"

// notes in the melody:
int melody[] = {
  NOTE_C4, NOTE_G3,NOTE_G3, NOTE_A3, NOTE_G3,0, NOTE_B3, NOTE_C4};

// note durations: 4 = quarter note, 8 = eighth note, etc.:
int noteDurations[] = {
  4, 8, 8, 4,4,4,4,4 };

void setup() {
  // iterate over the notes of the melody:
}

void loop() {
  // no need to repeat the melody.
  for (int thisNote = 0; thisNote < 8; thisNote++) {

    // to calculate the note duration, take one second 
    // divided by the note type.
    //e.g. quarter note = 1000 / 4, eighth note = 1000/8, etc.
    int noteDuration = 1000/noteDurations[thisNote];
    tone(2, melody[thisNote],noteDuration);

    // to distinguish the notes, set a minimum time between them.
    // the note's duration + 30% seems to work well:
    int pauseBetweenNotes = noteDuration * 1.30;
    delay(pauseBetweenNotes);
    // stop the tone playing:
    noTone(2);
  }
}
