# Fritzing sketch Attiny85-Dock (saved by Fritzing 0.8.0b)
breadboards: 1

parts:
  J2 = female pin header, 2 pins [form="♀ (female)"]  # not connected
  -_+ = female pin header, 2 pins [form="♀ (female)"]
  o_i = female pin header, 2 pins [form="♀ (female)"]
  -_+_2 = female pin header, 2 pins [form="♀ (female)"]
  i_o = female pin header, 2 pins [form="♀ (female)"]
  U1 = AMS1117 Voltage Regulator [package=SOT223]
  -_+_3 = female pin header, 2 pins [form="♀ (female)"]
  C1 = Electrolytic Capacitor [capacitance=1µF package="0405 [SMD, electrolytic]"]
  io_Power = female pin header, 2 pins [form="♀ (female)"]
  i_o3 = female pin header, 2 pins [form="♀ (female)"]
  Flip = female pin header, 2 pins [form="♀ (female)"]
  i_o5 = female pin header, 2 pins [form="♀ (female)"]

nets:
  N1: -_+.pin1, -_+_2.pin1
  N2: -_+.pin2, -_+_2.pin2, U1.output_voltage
  N3: o_i.pin1, i_o.pin2
  N4: o_i.pin2, i_o.pin1
  N5: U1.input_voltage, -_+_3.pin2, C1.+
  N6: io_Power.pin1, Flip.pin1
  N7: io_Power.pin2, Flip.pin2
  N8: i_o3.pin1, i_o5.pin1
  N9: i_o3.pin2, i_o5.pin2

notes:
  Radio
  Top
  >>>
  Processor
  >>
  - - - - - - - - - - - -
  5-16V
  clixx.io
  IoT Backplane
  r 0.2
  + -

custom parts:
  AMS1117 Voltage Regulator: 5V DC Voltage Regulator
