# Fritzing sketch Micro-FlatDock (saved by Fritzing 0.8.0b)
breadboards: 1

parts:
  -_+_*_i_o = female pin header, 5 pins [form="♀ (female)"]
  -_+_*_i_o_2 = female pin header, 5 pins [form="♀ (female)"]
  -_+_*_i_o_3 = female pin header, 5 pins [form="♀ (female)"]
  -_+_*_i_o_4 = female pin header, 5 pins [form="♀ (female)"]
  -_+_*_i_o_5 = female pin header, 5 pins [form="♀ (female)"]
  J1 = double row female pin header, 40 pins [form="♀ (female)"]  # not connected
  J2 = double row female pin header, 40 pins [form="♀ (female)"]  # not connected
  J3 = double row female pin header, 40 pins [form="♀ (female)"]  # not connected
  J4 = double row female pin header, 40 pins [form="♀ (female)"]  # not connected
  -_+_*_i_o_6 = female pin header, 5 pins [form="♀ (female)"]
  - = Pad [width=2 height=2 connect=center]
  + = Pad [width=2 height=2 connect=center]
  * = Pad [width=2 height=2 connect=center]
  i = Pad [width=2 height=2 connect=center]
  o = Pad [width=2 height=2 connect=center]
  -_2 = Pad [width=2 height=2 connect=center]
  o_2 = Pad [width=2 height=2 connect=center]
  i_2 = Pad [width=2 height=2 connect=center]
  *_2 = Pad [width=2 height=2 connect=center]
  +_2 = Pad [width=2 height=2 connect=center]
  *_3 = Pad [width=2 height=2 connect=center]
  o_3 = Pad [width=2 height=2 connect=center]
  i_3 = Pad [width=2 height=2 connect=center]
  -_3 = Pad [width=2 height=2 connect=center]
  +_3 = Pad [width=2 height=2 connect=center]
  -_4 = Pad [width=2 height=2 connect=center]
  o_4 = Pad [width=2 height=2 connect=center]
  i_4 = Pad [width=2 height=2 connect=center]
  *_4 = Pad [width=2 height=2 connect=center]
  +_4 = Pad [width=2 height=2 connect=center]
  *_5 = Pad [width=2 height=2 connect=center]
  i_5 = Pad [width=2 height=2 connect=center]
  -_5 = Pad [width=2 height=2 connect=center]
  +_5 = Pad [width=2 height=2 connect=center]
  o_5 = Pad [width=2 height=2 connect=center]
  *_6 = Pad [width=2 height=2 connect=center]
  i_6 = Pad [width=2 height=2 connect=center]
  -_6 = Pad [width=2 height=2 connect=center]
  +_6 = Pad [width=2 height=2 connect=center]
  o_6 = Pad [width=2 height=2 connect=center]

nets:
  N1: -_+_*_i_o.pin1, -.pad
  N2: -_+_*_i_o.pin2, -_+_*_i_o_2.pin2, -_+_*_i_o_3.pin2, -_+_*_i_o_4.pin4, -_+_*_i_o_5.pin4, -_+_*_i_o_6.pin2, +.pad, +_2.pad, +_3.pad, +_4.pad, +_5.pad, +_6.pad
  N3: -_+_*_i_o.pin3, *.pad
  N4: -_+_*_i_o.pin4, i.pad
  N5: -_+_*_i_o.pin5, o.pad
  N6: -_+_*_i_o_2.pin1, -_5.pad
  N7: -_+_*_i_o_2.pin3, *_5.pad
  N8: -_+_*_i_o_2.pin4, i_5.pad
  N9: -_+_*_i_o_2.pin5, o_5.pad
  N10: -_+_*_i_o_3.pin1, -_6.pad
  N11: -_+_*_i_o_3.pin3, *_6.pad
  N12: -_+_*_i_o_3.pin4, i_6.pad
  N13: -_+_*_i_o_3.pin5, o_6.pad
  N14: -_+_*_i_o_4.pin1, o_2.pad
  N15: -_+_*_i_o_4.pin2, i_2.pad
  N16: -_+_*_i_o_4.pin3, *_2.pad
  N17: -_+_*_i_o_4.pin5, -_2.pad
  N18: -_+_*_i_o_5.pin1, o_3.pad
  N19: -_+_*_i_o_5.pin2, i_3.pad
  N20: -_+_*_i_o_5.pin3, *_3.pad
  N21: -_+_*_i_o_5.pin5, -_3.pad
  N22: -_+_*_i_o_6.pin1, -_4.pad
  N23: -_+_*_i_o_6.pin3, *_4.pad
  N24: -_+_*_i_o_6.pin4, i_4.pad
  N25: -_+_*_i_o_6.pin5, o_4.pad

notes:
  Clixx.io
  MicroDock
  r 0.1
