# Fritzing sketch Adaptor-dual-side (saved by Fritzing 0.7.12b)
breadboards: 1

parts:
  J1 = double row female pin header, 4 pins [form="♀ (female)"]
  J2 = double row female pin header, 4 pins [form="♀ (female)"]

nets:
  N1: J1.pin1, J1.pin2
  N2: J1.pin3, J1.pin4
  N3: J2.pin1, J2.pin2
  N4: J2.pin3, J2.pin4

notes:
  clixx.io
  (c) 2014
