# Fritzing sketch InfraRedTransmitter (saved by Fritzing 0.7.12b)
breadboards: 1

parts:
  R1 = Resistor [tolerance=±5% resistance=100 package="0805 [SMD]"]
  o_i = female pin header, 2 pins [form="♀ (female)"]
  +_- = female pin header, 2 pins [form="♀ (female)"]
  i_o = female pin header, 2 pins [form="♀ (female)"]
  +_-_2 = female pin header, 2 pins [form="♀ (female)"]
  C1 = Tantalum Capacitor [capacitance=1µF package="A 3216 [SMD, tantalum]"]
  IR-TX = LED - 5mm [color="Red (633nm)" package="5 mm [THT]"]
  R2 = Resistor [tolerance=±5% resistance=100 package="0805 [SMD]"]
  Q1 = NPN-Transistor [part_number=2N2222A package="SOT-23 [SMD]"]
  IR-TX1 = LED - 5mm [color="Red (633nm)" package="5 mm [THT]"]
  IR-TX2 = LED - 5mm [color="Red (633nm)" package="5 mm [THT]"]
  R3 = Resistor [tolerance=±5% resistance=100 package="0805 [SMD]"]
  R4 = Resistor [tolerance=±5% resistance=100 package="0805 [SMD]"]

nets:
  N1: R1.Pin_0, Q1.0
  N2: R1.Pin_1, o_i.pin2
  N3: o_i.pin1, i_o.pin1
  5V: +_-.pin1, +_-_2.pin1, C1.+, R2.Pin_0, R3.Pin_0, R4.Pin_0
  GND: +_-.pin2, +_-_2.pin2, C1.-, Q1.2
  N4: IR-TX.cathode, Q1.1, IR-TX1.cathode, IR-TX2.cathode
  N5: IR-TX.anode, R2.Pin_1
  N6: IR-TX1.anode, R4.Pin_1
  N7: IR-TX2.anode, R3.Pin_1
