# Fritzing sketch Digital-output_LED (saved by Fritzing 0.8.0b)
breadboards: 1

parts:
  +_- = mystery part, 2 pins [chip_label=PWR-IN]
  o_i = mystery part, 2 pins [chip_label=DATA-IN]
  +_-_2 = mystery part, 2 pins [chip_label=PWR-OUT]
  i_o = mystery part, 2 pins [chip_label=DATA-OUT]
  R1 = Resistor [tolerance=±5% resistance=10k package="0805 [SMD]"]
  LED = LED - 5mm [color="Red (633nm)" package="5 mm [THT]"]
  Pad4 = Pad [width=2 height=3.7 connect=center]  # not connected
  Pad5 = Pad [width=2 height=3.7 connect=center]  # not connected
  Pad6 = Pad [width=2 height=3.7 connect=center]  # not connected
  Pad7 = Pad [width=2 height=3.7 connect=center]  # not connected

nets:
  GND: +_-.pin1, +_-_2.pin2, LED.cathode
  N1: +_-.pin2, +_-_2.pin1
  N2: o_i.pin1, i_o.pin2
  N3: o_i.pin2, i_o.pin1, R1.Pin_1
  N4: R1.Pin_0, LED.anode

notes:
  In this example, a pushbutton is used as a digital input and an LED is a digital output. Related example: http://arduino.cc/en/Tutorial/Button
  r 0.2
