# Fritzing sketch Digital-Potentiometer (saved by Fritzing 0.8.0b)
breadboards: 1

parts:
  +_- = mystery part, 2 pins [chip_label=PWR-IN]
  o_i = mystery part, 2 pins [chip_label=DATA-IN]
  + = female pin header, 1 pin [form="♀ (female)"]
  o = female pin header, 1 pin [form="♀ (female)"]
  - = female pin header, 1 pin [form="♀ (female)"]

nets:
  N1: +_-.pin1, -.pin1
  N2: +_-.pin2, +.pin1
  N3: o_i.pin1, o.pin1

notes:
  In this example, a pushbutton is used as a digital input and an LED is a digital output. Related example: http://arduino.cc/en/Tutorial/Button
  Potentiometer
  r 0.1
