# Fritzing sketch power-hbridge-TA8050p-n-mosfet (saved by Fritzing 0.7.12b)
breadboards: 1

parts:
  f_r = female pin header, 2 pins [form="♀ (female)"]
  +_- = female pin header, 2 pins [form="♀ (female)"]
  +_-_2 = Screw terminal - 2 pins [package=THT]
  +_-_3 = Screw terminal - 2 pins [package=THT]
  U3 = mystery part, 7 pins [chip_label=?]
  U5 = AMS1117 Voltage Regulator [package=SOT223]
  Q2 = NPN-Transistor [package="SOT-23 [SMD]"]
  Q3 = NPN-Transistor [package="SOT-23 [SMD]"]
  C1 = Tantalum Capacitor [capacitance=1µF package="A 3216 [SMD, tantalum]"]

nets:
  N1: f_r.pin1, Q2.0
  N2: f_r.pin2, Q3.0
  N3: +_-.pin1, U5.output_voltage
  GND: +_-.pin2, +_-_2.pin1, U3.pin4
  N4: +_-_2.pin2, U3.pin7, U5.input_voltage, C1.+
  N5: +_-_3.pin1, U3.pin3
  N6: +_-_3.pin2, U3.pin5
  N7: U3.pin1, Q2.1
  N8: U3.pin2, Q3.1

notes:
  Motor >>
  r0.1
  Power <<
  TA8050
  Motor Driver

custom parts:
  AMS1117 Voltage Regulator: 5V DC Voltage Regulator
