# Fritzing sketch power-hbridge-TA8050p (saved by Fritzing 0.8.0b)
breadboards: 1

parts:
  f_r = female pin header, 2 pins [form="♀ (female)"]
  +_- = female pin header, 2 pins [form="♀ (female)"]
  +_-_2 = Screw terminal - 2 pins [package=THT]
  +_-_3 = Screw terminal - 2 pins [package=THT]
  U3 = mystery part, 7 pins [chip_label=?]
  U5 = AMS1117 Voltage Regulator [package=SOT223]
  IC2 = BC857BS [chip_label=IC package=SMD]
  C1 = Tantalum Capacitor [capacitance=1µF package="B 3528 [SMD, tantalum]"]
  R1 = Resistor [tolerance=±5% resistance=220 package="0805 [SMD]"]
  R2 = Resistor [tolerance=±5% resistance=220 package="0805 [SMD]"]

nets:
  N1: f_r.pin1, R2.Pin_1
  N2: f_r.pin2, R1.Pin_1
  N3: +_-.pin1, U5.output_voltage
  GND: +_-.pin2
  N4: +_-_2.pin2, U3.pin7, U5.input_voltage, IC2.pin1, IC2.pin2, C1.+
  N5: +_-_3.pin1, U3.pin3
  N6: +_-_3.pin2, U3.pin5
  N7: U3.pin1, IC2.pin5
  N8: U3.pin2, IC2.pin4
  N9: IC2.pin3, R1.Pin_0
  N10: IC2.pin6, R2.Pin_0

notes:
  Motor >>
  r0.1
  Power <<
  TA8050
  Motor Driver

custom parts:
  AMS1117 Voltage Regulator: 5V DC Voltage Regulator
  BC857BS: A DIP stand-in part for whatever IC you want. With 8 pins on a 300mil dual inline package (DIP) footprint.
