# Fritzing sketch power-ams1117 (saved by Fritzing 0.7.12b)
breadboards: 1

parts:
  o_i = female pin header, 2 pins [form="♀ (female)"]
  +_- = female pin header, 2 pins [form="♀ (female)"]
  R2 = Resistor [tolerance=±5% resistance=220 package="0805 [SMD]"]
  R1 = Resistor [tolerance=±5% resistance=220 package="0805 [SMD]"]
  -_+ = Screw terminal - 2 pins [package=THT]
  U2 = Voltage Regulator - 5V [part_number=LT1086 package=TO-220]
  C1 = Electrolytic Capacitor [capacitance=1µF package="100 mil [THT, electrolytic]"]
  R3 = Resistor [tolerance=±5% resistance=220 package="0805 [SMD]"]
  R4 = Resistor [tolerance=±5% resistance=220 package="0805 [SMD]"]

nets:
  N1: o_i.pin1, R3.Pin_0, R4.Pin_1
  N2: +_-.pin1, R2.Pin_0, U2.output_voltage, C1.+
  GND: +_-.pin2, R1.Pin_0
  N3: R2.Pin_1, R1.Pin_1
  N4: -_+.pin1, U2.input_voltage, R3.Pin_1
  N5: U2.GND, C1.-

notes:
  16V Max
  r0.2
  Power
  -     +
  GND
  Regulator

custom parts:
  Voltage Regulator - 5V: 5V DC Voltage Regulator
