# Fritzing sketch power-vreg-and-mosfet-n (saved by Fritzing 0.8.0b)
breadboards: 1

parts:
  o_i = female pin header, 2 pins [form="♀ (female)"]
  +_- = female pin header, 2 pins [form="♀ (female)"]
  R2 = Resistor [tolerance=±5% resistance=220 package="0805 [SMD]"]
  R1 = Resistor [tolerance=±5% resistance=220 package="0805 [SMD]"]
  -_+ = Screw terminal - 2 pins [package=THT]
  U2 = Voltage Regulator - 5V [part_number=LT1086 package=TO-220]
  C1 = Electrolytic Capacitor [capacitance=1µF package="100 mil [THT, electrolytic]"]
  R3 = Resistor [tolerance=±5% resistance=220 package="0805 [SMD]"]
  R4 = Resistor [tolerance=±5% resistance=220 package="0805 [SMD]"]
  -_+_2 = Screw terminal - 2 pins [package=THT]
  R5 = Resistor [tolerance=±5% resistance=220 package="0805 [SMD]"]
  n-Channel_Mosfet = Basic FET N-Channel [package="TO220 [THT]"]

nets:
  N1: o_i.pin1, R3.Pin_0, R4.Pin_1
  N2: o_i.pin2, R5.Pin_0, n-Channel_Mosfet.gate
  N3: +_-.pin1, U2.GND
  GND: +_-.pin2, R1.Pin_0, R5.Pin_1
  N4: R2.Pin_0, U2.output_voltage, C1.+
  N5: R2.Pin_1, R1.Pin_1
  N6: -_+.pin1, U2.input_voltage, R3.Pin_1, -_+_2.pin1
  N7: -_+.pin2, n-Channel_Mosfet.source
  N8: -_+_2.pin2, n-Channel_Mosfet.drain

notes:
  Ouput >>
  r0.1
  Power <<
  - +
  +>>

custom parts:
  Voltage Regulator - 5V: 5V DC Voltage Regulator
