# Fritzing sketch power-dock-spx1117 (saved by Fritzing 0.9.2b)
circuit board: 2.92478cm x 5.58617cm
breadboards: 1

parts:
  +_- = mystery part, 2 pins [chip_label=PWR-OUT]
  i_o = mystery part, 2 pins [chip_label=DATA-OUT]  # not connected
  Pad2 = Pad [width=1.22296296296297 height=3.19851851851851 connect=center]  # not connected
  Pad1 = Pad [width=1.22296296296297 height=3.19851851851851 connect=center]  # not connected
  Pad4 = Pad [width=1.22296296296297 height=3.19851851851851 connect=center]
  Pad3 = Pad [width=1.22296296296297 height=3.19851851851851 connect=center]  # not connected
  Pad5 = Pad [width=2 height=4.5 connect=center]  # not connected
  Pad6 = Pad [width=2 height=4.5 connect=center]  # not connected
  J1 = screw terminal, 2 pins
  IC1 = Voltage Regulator LM1117 [package=sot223]
  J2 = female pin header, 2 pins [form="♀ (female)"]
  C1 = Electrolytic Capacitor [capacitance=0.1mF package="0405 [SMD, electrolytic]"]
  R1 = Resistor [tolerance=±5% resistance=220 package="0805 [SMD]"]
  LED1 = smd LED [color="Red (633nm)" package="0805 [SMD]"]

nets:
  N1: +_-.pin1, IC1.OUT, R1.Pin_0
  N2: +_-.pin2, Pad4.pad, J1.pin2, IC1.ADJ, C1.-, LED1.anode
  N3: J1.pin1, J2.pin2, C1.+
  N4: IC1.IN, J2.pin1
  N5: R1.Pin_1, LED1.cathode

notes:
  In this example, a pushbutton is used as a digital input and an LED is a digital output. Related example: http://arduino.cc/en/Tutorial/Button
  r0.1
  clixx.io
  Power
  +
  -
