# Fritzing sketch Attiny-8pin-sop (saved by Fritzing 0.8.0b)
breadboards: 1

parts:
  i_o = female pin header, 2 pins [form="♀ (female)"]
  clixx_io = Tantalum Capacitor [capacitance="1 μF" package="A 3216 [SMD, tantalum]"]
  Digital-1 = female pin header, 5 pins [form="♀ (female)"]
  Digital-2 = female pin header, 5 pins [form="♀ (female)"]
  -_+ = female pin header, 2 pins [form="♀ (female)"]
  + = Pad [width=1 height=3 connect=center]
  - = Pad [width=1 height=3 connect=center]
  o = Pad [width=1 height=3 connect=center]
  i = Pad [width=1 height=3 connect=center]
  Pad1 = Pad [width=0.7 height=1.5 connect=center]
  Pad4 = Pad [width=0.7 height=1.5 connect=center]
  Pad5 = Pad [width=0.7 height=1.5 connect=center]
  Pad6 = Pad [width=0.7 height=1.5 connect=center]
  Pad7 = Pad [width=0.7 height=1.5 connect=center]
  Pad8 = Pad [width=0.7 height=1.5 connect=center]
  Pad2 = Pad [width=0.7 height=1.5 connect=center]
  Pad3 = Pad [width=0.7 height=1.5 connect=center]
  Pad9 = Pad [width=1.7 height=4 connect=center]  # not connected
  Pad10 = Pad [width=1.7 height=4 connect=center]  # not connected
  R1 = Resistor [tolerance=±5% resistance=220 package="0805 [SMD]"]
  +_- = female pin header, 2 pins [form="♀ (female)"]
  Attiny = AVR Attiny [package="DIP (Dual Inline) [THT]"]

nets:
  N1: i_o.pin1, Digital-1.pin1, Pad6.pad, Attiny.pin6
  N2: i_o.pin2, Digital-1.pin2, Pad7.pad, Attiny.pin7
  GND: clixx_io.-, +_-.pin2
  N3: clixx_io.+, Digital-1.pin4, Digital-2.pin4, -_+.pin2, +.pad, R1.Pin_0, +_-.pin1, Attiny.pin8
  N4: Digital-1.pin3, Pad1.pad, R1.Pin_1, Attiny.pin1
  N5: Digital-1.pin5, Digital-2.pin5, -_+.pin1, -.pad, Pad4.pad, Pad8.pad, Attiny.pin4
  N6: Digital-2.pin1, i.pad, Pad2.pad, Attiny.pin2
  N7: Digital-2.pin2, o.pad, Pad3.pad, Attiny.pin3
  N8: Digital-2.pin3, Pad5.pad, Attiny.pin5

notes:
  o
  *
  i
  -
  +
  i=PB2
  o=PB1
  *=PB5
  i=PB3
  o=PB4
  *=PB0
  r0.3
  85

custom parts:
  AVR Attiny: Attiny85 SOP8
