# Fritzing sketch Processor-Atmega328p-28p-Flat (saved by Fritzing 0.7.12b)
breadboards: 1

parts:
  LED1 = LED - 5mm [color="Red (633nm)" package="5 mm [THT]"]
  R3 = Resistor [tolerance=±5% resistance=1k package="0805 [SMD]"]  # not connected
  R2 = Resistor [tolerance=±5% resistance=2.2k package="0805 [SMD]"]  # not connected
  R7 = Resistor [tolerance=±5% resistance=220 package="0805 [SMD]"]
  U1 = atmega328 [package=dip]
  R8 = Resistor [tolerance=±5% resistance=1k package="0805 [SMD]"]
  - = Pad [width=1.25 height=2.54 connect=center]  # not connected
  Pad3 = Pad [width=1.25 height=2.54 connect=center]
  Pad4 = Pad [width=1.25 height=2.54 connect=center]  # not connected
  Pad5 = Pad [width=1.25 height=2.54 connect=center]
  Pad6 = Pad [width=1.25 height=2.54 connect=center]
  Pad7 = Pad [width=1.25 height=2.54 connect=center]  # not connected
  Pad8 = Pad [width=1.25 height=2.54 connect=center]
  Pad9 = Pad [width=1.25 height=2.54 connect=center]  # not connected
  Pad10 = Pad [width=1.25 height=2.54 connect=center]  # not connected
  Pad11 = Pad [width=1.25 height=2.54 connect=center]  # not connected
  Pad12 = Pad [width=1.25 height=2.54 connect=center]  # not connected
  Pad13 = Pad [width=1.25 height=2.54 connect=center]
  Pad14 = Pad [width=1.25 height=2.54 connect=center]  # not connected
  Pad15 = Pad [width=1.25 height=2.54 connect=center]  # not connected
  Pad16 = Pad [width=1.25 height=2.54 connect=center]  # not connected
  Pad18 = Pad [width=1.25 height=2.54 connect=center]  # not connected
  -1 = Pad [width=1.25 height=2.54 connect=center]  # not connected
  Pad28 = Pad [width=1.25 height=2.54 connect=center]  # not connected
  Pad24 = Pad [width=1.25 height=2.54 connect=center]  # not connected
  Pad29 = Pad [width=1.25 height=2.54 connect=center]
  Pad30 = Pad [width=1.25 height=2.54 connect=center]  # not connected
  Pad20 = Pad [width=1.25 height=2.54 connect=center]  # not connected
  Pad21 = Pad [width=1.25 height=2.54 connect=center]  # not connected
  Pad27 = Pad [width=1.25 height=2.54 connect=center]
  Pad22 = Pad [width=1.25 height=2.54 connect=center]  # not connected
  Pad17 = Pad [width=1.25 height=2.54 connect=center]  # not connected
  Pad25 = Pad [width=1.25 height=2.54 connect=center]  # not connected
  Pad23 = Pad [width=1.25 height=2.54 connect=center]  # not connected
  Pad19 = Pad [width=1.25 height=2.54 connect=center]
  Pad26 = Pad [width=1.25 height=2.54 connect=center]  # not connected
  Pad31 = Pad [width=1.25 height=2.54 connect=center]  # not connected
  Pad32 = Pad [width=1.25 height=2.54 connect=center]
  -2 = Pad [width=1.25 height=2.54 connect=center]
  Pad33 = Pad [width=1.25 height=2.54 connect=center]  # not connected

nets:
  N1: LED1.anode, R7.Pin_0
  N2: U1.RESET, R8.Pin_0
  N3: U1.D0_(RX), Pad3.pad
  N4: U1.D1_(TX), Pad6.pad
  N5: U1.VCC, U1.AVCC, U1.AREF, R8.Pin_1, Pad5.pad, Pad8.pad, Pad13.pad, Pad29.pad, Pad27.pad, Pad19.pad, Pad32.pad, -2.pad

notes:
  -
  i
  o
  +
  *
  d
  c
  Analog 1
  Analog 2
  o - D5 (PWM)
  i - A0 (ADC)
  o - D9 (PWM)
  i - A1 (ADC)
  Digital 1
  Digital 2
  Digital 3
  i - D4
  o - D3
  i - D12
  o - D13
  i - D10
  o - D8 (3.3v)
  I2C
  SDA - A4
  * - D2
  SCL - A5
  clixx.io
  * - D11
  * - D6 (PWM)
