# Fritzing sketch radio-ESP2866 (saved by Fritzing 0.7.12b)
breadboards: 1

parts:
  o_i = mystery part, 2 pins [chip_label=DATA-IN]
  +_- = mystery part, 2 pins [chip_label=PWR-OUT]
  i_o = mystery part, 2 pins [chip_label=DATA-OUT]
  -_+ = mystery part, 2 pins [chip_label=PWR-IN]
  ESP2866 = double row female pin header, 8 pins [form="♀ (female)"]
  Pad2 = Pad [width=2 height=3.7 connect=center]  # not connected
  Pad3 = Pad [width=2 height=3.7 connect=center]  # not connected
  Pad4 = Pad [width=2 height=3.7 connect=center]  # not connected
  Pad5 = Pad [width=2 height=3.7 connect=center]  # not connected
  C1 = Electrolytic Capacitor [capacitance=1µF package="0405 [SMD, electrolytic]"]

nets:
  N1: o_i.pin1, ESP2866.pin1
  N2: o_i.pin2, ESP2866.pin5
  N3: +_-.pin1, -_+.pin1, ESP2866.pin2, ESP2866.pin4, C1.+
  N4: +_-.pin2, -_+.pin2, ESP2866.pin8, C1.-
  N5: i_o.pin1, ESP2866.pin6
  N6: i_o.pin2, ESP2866.pin7

notes:
  In this example, a pushbutton is used as a digital input and an LED is a digital output. Related example: http://arduino.cc/en/Tutorial/Button
  Wifi
