# Fritzing sketch convertor-usb-ttl-ch340g (saved by Fritzing 0.9.2b)
circuit board: 2.92478cm x 5.58617cm
breadboards: 1

parts:
  +_- = mystery part, 2 pins [chip_label=PWR-OUT]
  i_o = mystery part, 2 pins [chip_label=DATA-OUT]
  Pad2 = Pad [width=1.22296296296297 height=3.19851851851851 connect=center]  # not connected
  Pad1 = Pad [width=1.22296296296297 height=3.19851851851851 connect=center]  # not connected
  Pad4 = Pad [width=1.22296296296297 height=3.19851851851851 connect=center]  # not connected
  Pad3 = Pad [width=1.22296296296297 height=3.19851851851851 connect=center]  # not connected
  J1 = rounded female pin header, 6 pins [form="♀ (female rounded)"]
  part = rounded female pin header, 6 pins [form="♀ (female rounded)"]  # not connected
  IC1 = Voltage Regulator LM1117 [package=sot223]
  Pad5 = Pad [width=2 height=4.5 connect=center]  # not connected
  Pad6 = Pad [width=2 height=4.5 connect=center]  # not connected

nets:
  N1: +_-.pin1, IC1.OUT
  N2: +_-.pin2, J1.pin6, IC1.ADJ
  N3: i_o.pin1, J1.pin4
  N4: i_o.pin2, J1.pin5
  N5: J1.pin1, IC1.IN
  N6: J1.pin2, J1.pin3

notes:
  In this example, a pushbutton is used as a digital input and an LED is a digital output. Related example: http://arduino.cc/en/Tutorial/Button
  r0.2
  Adaptor
  clixx.io
  USB Serial
  3.3V
