# Fritzing sketch convertor-usb-ttl (saved by Fritzing 0.8.3b)
circuit board: 2.92478cm x 5.58617cm
breadboards: 1

parts:
  +_- = mystery part, 2 pins [chip_label=PWR-OUT]
  i_o = mystery part, 2 pins [chip_label=DATA-OUT]
  Pad2 = Pad [width=1.22296296296297 height=3.19851851851851 connect=center]  # not connected
  Pad1 = Pad [width=1.22296296296297 height=3.19851851851851 connect=center]  # not connected
  Pad4 = Pad [width=1.22296296296297 height=3.19851851851851 connect=center]  # not connected
  Pad3 = Pad [width=1.22296296296297 height=3.19851851851851 connect=center]  # not connected
  J1 = rounded female pin header, 5 pins [form="♀ (female rounded)"]

nets:
  N1: +_-.pin1, J1.pin1
  N2: +_-.pin2, J1.pin5
  N3: i_o.pin1, J1.pin3
  N4: i_o.pin2, J1.pin4

notes:
  In this example, a pushbutton is used as a digital input and an LED is a digital output. Related example: http://arduino.cc/en/Tutorial/Button
  r0.1
  Adaptor
  clixx.io
  USB Serial
  3.3V
